# Fritzing sketch Connector (saved by Fritzing 0.7.12b)
breadboards: 1

parts:
  Power = Generic 2 pin connector [form="♀ (female)" package=THT]
  R2 = Resistor [tolerance=±5% resistance=1k package=THT]
  Power_2 = LED - 5mm [color="Green (570nm)" package="5 mm [THT]"]
  Arduino1 = Arduino
  I2C_Power = Generic 2 pin connector [form="♀ (female)" package=THT]
  I2C = Generic 2 pin connector [form="♀ (female)" package=THT]
  R3 = Resistor [tolerance=±5% resistance=1.5k package=THT]
  R4 = Resistor [tolerance=±5% resistance=1.5k package=THT]
  Area_1 = Generic 2 pin connector [form="♀ (female)" package=THT]
  R5 = Resistor [tolerance=±5% resistance=680 package=THT]
  V_Ext = LED - 5mm [color="Yellow (585nm)" package="5 mm [THT]"]
  Area_2 = Generic 2 pin connector [form="♀ (female)" package=THT]
  R6 = Resistor [tolerance=±5% resistance=220 package=THT]
  Armed = LED - 5mm [color="Red (633nm)" package="5 mm [THT]"]
  V_Ext_2 = Generic 2 pin connector [form="♀ (female)" package=THT]
  CP_2 = Generic 2 pin connector [form="♀ (female)" package=THT]
  CP_1 = Generic 2 pin connector [form="♀ (female)" package=THT]
  Alarm = Generic 2 pin connector [form="♀ (female)" package=THT]
  R7 = Resistor [tolerance=±5% resistance=100 package=THT]
  Adv = Generic 2 pin connector [form="♀ (female)" package=THT]
  R10 = Resistor [tolerance=±5% resistance=220 package=THT]
  R11 = Resistor [tolerance=±5% resistance=220 package=THT]
  J18 = female pin header, 3 pins [form="♀ (female)"]

nets:
  N1: Power.Pin_1, R2.Pin_1, Arduino1.VIN, R10.Pin_0
  N2: Power.Pin_2, Power_2.cathode, Arduino1.GND, I2C_Power.Pin_2, V_Ext.cathode, Armed.cathode, V_Ext_2.Pin_2, Alarm.Pin_1
  N3: R2.Pin_0, Power_2.anode
  N4: Arduino1.D13, R6.Pin_0, CP_2.Pin_2
  N5: Arduino1.D12, Area_2.Pin_2
  N6: Arduino1.D11, Area_1.Pin_2
  N7: Arduino1.D10, Alarm.Pin_2
  N8: Arduino1.D6, Adv.Pin_1
  N9: Arduino1.D5, R7.Pin_0
  N10: Arduino1.D4, J18.pin3
  N11: Arduino1.D3, R5.Pin_0, V_Ext_2.Pin_1, J18.pin2
  N12: Arduino1.D2, CP_1.Pin_2
  N13: Arduino1.+5V, R3.Pin_1, R4.Pin_1, R11.Pin_0
  N14: Arduino1.A0, Area_1.Pin_1
  N15: Arduino1.A1, Area_2.Pin_1
  N16: Arduino1.A2, CP_2.Pin_1
  N17: Arduino1.A3, Adv.Pin_2
  N18: Arduino1.A4, I2C.Pin_1, R3.Pin_0
  N19: Arduino1.A5, I2C.Pin_2, R4.Pin_0
  N20: I2C_Power.Pin_1, R10.Pin_1
  N21: R5.Pin_1, V_Ext.anode
  N22: R6.Pin_1, Armed.anode
  N23: CP_1.Pin_1, R7.Pin_1
  N24: R11.Pin_1, J18.pin1

notes:
  Home Security
  Alberto Crespo
