# Fritzing sketch Raspery to arduino (saved by Fritzing 0.7.12b)
breadboards: 1

parts:
  Arduino1 = Arduino
  Raspberry_Pi1 = Raspberry Pi (Model B)

nets:
  GND: Arduino1.GND, Raspberry_Pi1.GND
  N1: Arduino1.D2, Raspberry_Pi1.#17
  N2: Arduino1.D1TX, Raspberry_Pi1.SCLK
  N3: Arduino1.D0RX, Raspberry_Pi1.RXD
  3V3: Arduino1.3V3, Raspberry_Pi1.3V3
  +5V: Arduino1.+5V, Raspberry_Pi1.5V
  N4: Arduino1.SCL, Raspberry_Pi1.SCL
  N5: Arduino1.SDA, Raspberry_Pi1.SDA

custom parts:
  Raspberry Pi (Model B): Raspberry Pi Single-board Computer, Model B
