# Fritzing sketch Remote Terminal (saved by Fritzing 0.7.12b)
breadboards: 1

parts:
  U2 = PCF8574 [package="DIP16 [THT]"]
  Area_1 = Generic 2 pin connector [form="♀ (female)" package=THT]
  Area_2 = Generic 2 pin connector [form="♀ (female)" package=THT]
  Area_3 = Generic 2 pin connector [form="♀ (female)" package=THT]
  Area_4 = Generic 2 pin connector [form="♀ (female)" package=THT]
  R1 = Resistor [tolerance=±5% resistance=220 package=THT]
  Vin = LED - 5mm [color="Red (633nm)" package="5 mm [THT]"]
  P_OUT = Generic 2 pin connector [form="♀ (female)" package=THT]
  R2 = Resistor [tolerance=±5% resistance=220 package=THT]
  A2 = female pin header, 3 pins [form="♀ (female)"]
  A1 = female pin header, 3 pins [form="♀ (female)"]
  A0 = female pin header, 3 pins [form="♀ (female)"]
  C1 = Ceramic Capacitor [capacitance=100nF package="200 mil [THT, multilayer]"]
  IN = female pin header, 4 pins [form="♀ (female)"]
  OUT = female pin header, 4 pins [form="♀ (female)"]
  P_IN = Generic 2 pin connector [form="♀ (female)" package=THT]
  I2C_+_INT = Generic 3 pin connector [form="♀ (female)" package=THT]

nets:
  N1: U2.A0, A0.pin2
  N2: U2.A1, A1.pin2
  N3: U2.A3, A2.pin2
  N4: U2.P0, Area_1.Pin_1, IN.pin1
  N5: U2.P1, Area_1.Pin_2, IN.pin2
  N6: U2.P2, Area_2.Pin_1, IN.pin3
  N7: U2.P3, Area_2.Pin_2, IN.pin4
  N8: U2.GND, Vin.cathode, P_OUT.Pin_2, A2.pin3, A1.pin3, A0.pin3, C1.0, P_IN.Pin_2
  N9: U2.P4, Area_3.Pin_1, OUT.pin4
  N10: U2.P5, Area_3.Pin_2, OUT.pin3
  N11: U2.P6, Area_4.Pin_1, OUT.pin2
  N12: U2.P7, Area_4.Pin_2, OUT.pin1
  N13: U2.INT, I2C_+_INT.Pin_1
  N14: U2.SCL, I2C_+_INT.Pin_2
  N15: U2.SDA, I2C_+_INT.Pin_3
  N16: U2.VCC, R1.Pin_1, R2.Pin_0, A2.pin1, A1.pin1, A0.pin1, C1.1, P_IN.Pin_1
  N17: R1.Pin_0, Vin.anode
  N18: P_OUT.Pin_1, R2.Pin_1

notes:
  Alberto Crespo
  HSRT

custom parts:
  Generic 3 pin connector: Generic 2 pin connector
